# Fritzing sketch LV15_Project3 (saved by Fritzing 0.9.1b)
breadboards: 1

parts:
  Raspberry_Pi1 = Raspberry Pi B+
  S1 = Momentary Switch [package=ksa_sealed_tac_switch]

nets:
  N1: Raspberry_Pi1.GPIO26, S1.1
  N2: Raspberry_Pi1.GND, S1.3
